// Logisim project elevstorSelect.circ as structural Verilog: 1 circuit, main circuit main
module main (
  input  B1
);

  wire and_1_out, and_2_out, and_3_out, and_4_out, and_5_out, and_6_out, and_8_out, and_9_out, and_10_out,
       and_11_out, and_12_out, and_14_out, and_15_out, and_16_out, and_17_out, and_18_out, and_20_out,
       and_21_out, and_22_out, and_23_out, and_24_out, and_25_out, and_26_out, and_27_out, and_28_out,
       and_29_out, and_30_out, C1, C2, C3, C4, E1BiggerUseE2, eqE2bigUseE1, multiplexer_1_out,
       multiplexer_2_out, multiplexer_3_out, multiplexer_4_out, nor_1_out, not_1_out, not_2_out, not_3_out,
       not_4_out, not_5_out, not_6_out, not_7_out, not_8_out, not_9_out, not_10_out, not_11_out, not_12_out,
       or_1_out, or_2_out, or_3_out, or_4_out, or_9_out, or_10_out, or_11_out, or_12_out, PorN, PorN2, X0,
       X1, xor_1_out, xor_2_out, xor_3_out, xor_4_out, xor_5_out, xor_6_out, xor_7_out, xor_8_out, xor_9_out,
       xor_10_out, xor_11_out, xor_12_out, Y0, Y1;

  not not_1 (not_1_out, 1'b0);
  not not_2 (not_2_out, 1'b0);
  not not_3 (not_3_out, 1'b1);
  not not_4 (not_4_out, 1'b1);
  xor xor_1 (xor_1_out, B1, not_1_out);
  and and_1 (and_1_out, B1, not_1_out);
  and and_2 (and_2_out, B1, C1);
  and and_3 (and_3_out, not_1_out, C1);
  xor xor_2 (xor_2_out, 1'b0, not_2_out);
  and and_4 (and_4_out, 1'b0, not_2_out);
  and and_5 (and_5_out, 1'b0, 1'b1);
  and and_6 (and_6_out, not_2_out, 1'b1);
  xor xor_3 (xor_3_out, B1, not_3_out);
  // AND_Gate and_7 has open pins: in0=B1, in1=not_3_out, out=open
  and and_8 (and_8_out, B1, C2);
  and and_9 (and_9_out, not_3_out, C2);
  xor xor_4 (xor_4_out, 1'b0, not_4_out);
  and and_10 (and_10_out, 1'b0, not_4_out);
  and and_11 (and_11_out, 1'b0, 1'b1);
  and and_12 (and_12_out, not_4_out, 1'b1);
  LED led_1 (.in(E1BiggerUseE2));
  or or_1 (or_1_out, and_2_out, and_3_out);
  or or_2 (or_2_out, and_5_out, and_6_out);
  LED led_2 (.in(eqE2bigUseE1));
  or or_3 (or_3_out, and_8_out, and_9_out);
  or or_4 (or_4_out, and_11_out, and_12_out);
  or or_5 (PorN, and_1_out, or_1_out);
  or or_6 (C1, and_4_out, or_2_out);
  or or_7 (C2, and_10_out, or_4_out);
  buf or_8 (PorN2, or_3_out);  // OR_Gate
  xor xor_5 (xor_5_out, xor_1_out, C1);
  xor xor_6 (xor_6_out, xor_2_out, 1'b1);
  xor xor_7 (xor_7_out, xor_3_out, C2);
  xor xor_8 (xor_8_out, xor_4_out, 1'b1);
  not not_5 (not_5_out, xor_5_out);
  not not_6 (not_6_out, xor_6_out);
  LED led_3 (.in(E1BiggerUseE2));
  LED led_4 (.in(eqE2bigUseE1));
  Multiplexer multiplexer_1 (.in0(xor_5_out), .in1(not_5_out), .out(multiplexer_1_out), .sel(PorN));
  Multiplexer multiplexer_2 (.in0(xor_6_out), .in1(not_6_out), .out(multiplexer_2_out), .sel(PorN));
  not not_7 (not_7_out, xor_7_out);
  not not_8 (not_8_out, xor_8_out);
  Multiplexer multiplexer_3 (.in0(xor_8_out), .in1(not_8_out), .out(multiplexer_3_out), .sel(PorN2));
  Multiplexer multiplexer_4 (.in0(xor_7_out), .in1(not_7_out), .out(multiplexer_4_out), .sel(PorN2));
  xor xor_9 (xor_9_out, multiplexer_1_out, 1'b0);
  // AND_Gate and_13 has open pins: in0=multiplexer_1_out, in1=1'b0, out=open
  and and_14 (and_14_out, multiplexer_1_out, C3);
  and and_15 (and_15_out, 1'b0, C3);
  and and_16 (and_16_out, multiplexer_2_out, PorN);
  and and_17 (and_17_out, multiplexer_2_out, 1'b0);
  and and_18 (and_18_out, PorN, 1'b0);
  xor xor_10 (xor_10_out, multiplexer_4_out, 1'b0);
  // AND_Gate and_19 has open pins: in0=multiplexer_4_out, in1=1'b0, out=open
  and and_20 (and_20_out, multiplexer_4_out, C4);
  and and_21 (and_21_out, 1'b0, C4);
  and and_22 (and_22_out, multiplexer_3_out, PorN2);
  and and_23 (and_23_out, multiplexer_3_out, 1'b0);
  and and_24 (and_24_out, PorN2, 1'b0);
  xor xor_11 (xor_11_out, multiplexer_2_out, PorN);
  xor xor_12 (xor_12_out, multiplexer_3_out, PorN2);
  or or_9 (or_9_out, and_14_out, and_15_out);
  or or_10 (or_10_out, and_17_out, and_18_out);
  or or_11 (or_11_out, and_20_out, and_21_out);
  or or_12 (or_12_out, and_23_out, and_24_out);
  or or_13 (C3, and_16_out, or_10_out);
  or or_14 (C4, and_22_out, or_12_out);
  xor xor_13 (X1, xor_9_out, C3);
  xor xor_14 (X0, xor_11_out, 1'b0);
  xor xor_15 (Y1, xor_10_out, C4);
  xor xor_16 (Y0, xor_12_out, 1'b0);
  not not_9 (not_9_out, X1);
  not not_10 (not_10_out, X0);
  not not_11 (not_11_out, Y1);
  not not_12 (not_12_out, Y0);
  and and_25 (and_25_out, X1, not_11_out);
  and and_26 (and_26_out, X1, not_12_out, X0);
  and and_27 (and_27_out, X0, not_12_out, not_11_out);
  and and_28 (and_28_out, not_9_out, Y1);
  and and_29 (and_29_out, not_9_out, Y0, not_10_out);
  and and_30 (and_30_out, Y1, Y0, not_10_out);
  or or_15 (E1BiggerUseE2, and_25_out, and_26_out, and_27_out);
  or or_16 (eqE2bigUseE1, and_28_out, and_29_out, and_30_out);
  LED led_5 (.in(E1BiggerUseE2));
  nor nor_1 (nor_1_out, E1BiggerUseE2, eqE2bigUseE1);
  LED led_6 (.in(eqE2bigUseE1));
endmodule
